# Fritzing sketch PCB (saved by Fritzing 0.9.4)
circuit board: 4.82cm x 6cm
breadboards: 1

parts:
  ESP8266 = NodeMCU V1.0
  Temp- = Momentary Switch [package=ksa_sealed_tac_switch]
  On/Off = Momentary Switch [package=ksa_sealed_tac_switch]
  Temp+ = Momentary Switch [package=ksa_sealed_tac_switch]
  R2 = Resistor [tolerance=±5% resistance=10k package=THT]
  R3 = Resistor [tolerance=±5% resistance=10k package=THT]
  R4 = Resistor [tolerance=±5% resistance=10k package=THT]
  RELAY = Header 3 [package=jst-3-pth]
  PROBE = Header 3 [package=jst-3-pth]
  +_-_D_C = Header 4 [package=molex-1x4_lock]

nets:
  N1: ESP8266.D1, +_-_D_C.4
  N2: ESP8266.D2, +_-_D_C.3
  N3: ESP8266.D3, RELAY.1
  N4: ESP8266.D4, PROBE.1
  N5: ESP8266.3V3, Temp-.3, Temp-.4, On/Off.3, On/Off.4, Temp+.3, Temp+.4, RELAY.2, PROBE.2, +_-_D_C.1
  N6: ESP8266.GND, R2.Pin_0, R3.Pin_0, R4.Pin_0, RELAY.3, PROBE.3, +_-_D_C.2
  N7: ESP8266.D5, Temp+.1, Temp+.2, R4.Pin_1
  N8: ESP8266.D6, Temp-.1, Temp-.2, R3.Pin_1
  N9: ESP8266.D7, On/Off.1, On/Off.2, R2.Pin_1

custom parts:
  NodeMCU V1.0: ESP8266 based NodeMCU
